# Fritzing sketch schematics (saved by Fritzing 0.9.3b)
breadboards: 1

parts:
  Raspberry_Pi_Zero1 = Raspberry Pi Zero
  J1 = Basic Servo
  S1 = Pushbutton [package="[THT]"]
  J2 = Basic Servo
  VCC1 = Battery block 9V
  Part1 = Breadboard Power Supply Board SMD
  J3 = Infrared Proximity Sensor

nets:
  GND: Raspberry_Pi_Zero1.GPIO2, Raspberry_Pi_Zero1.GND, J1.gnd, S1.Pin_1, S1.Pin_2, S1.Pin_3, S1.Pin_4, J2.gnd, VCC1.-, Part1.GND, J3.GND
  N1: Raspberry_Pi_Zero1.GPIO3, J3.Vout
  VCC: Raspberry_Pi_Zero1.GPIO19, J1.vcc, J2.vcc, J2.pulse, Part1.VCC, J3.Vcc
  N2: Raspberry_Pi_Zero1.GPIO26, J1.pulse
  N3: VCC1.+, Part1.VIN
