# Fritzing sketch schematics (saved by Fritzing 0.9.3b)
breadboards: 1

parts:
  Raspberry_Pi_Zero1 = Raspberry Pi Zero
  J1 = Basic Servo
  S1 = Pushbutton [package="[THT]"]
  J2 = Basic Servo
  VCC1 = Battery block 9V
  Part1 = Breadboard Power Supply Board SMD
  Part2 = Adafruit ADS1115 16Bit I2C ADC [part_number="Adafruit #1085"]
  hc-sr1 = hc-sr04
  R2 = Resistor [tolerance=±5% resistance=1k package=THT]
  R3 = Resistor [tolerance=±5% resistance=2k package=THT]
  LED1 = LED - 5mm [color="Infrared (850nm)" package="5 mm [THT]"]
  R4 = Photocell (LDR) [package=THT]
  LED2 = LED - 5mm [color="Infrared (850nm)" package="5 mm [THT]"]
  R5 = Photocell (LDR) [package=THT]
  LED3 = LED - 5mm [color="Infrared (850nm)" package="5 mm [THT]"]
  R6 = Photocell (LDR) [package=THT]
  R7 = Resistor [tolerance=±5% resistance=270 package=THT]
  R8 = Resistor [tolerance=±5% resistance=270 package=THT]
  R9 = Resistor [tolerance=±5% resistance=270 package=THT]
  LED4 = LED - 5mm [color="Infrared (850nm)" package="5 mm [THT]"]
  R10 = Photocell (LDR) [package=THT]
  R11 = Resistor [tolerance=±5% resistance=270 package=THT]

nets:
  N1: Raspberry_Pi_Zero1.GPIO2, Part2.SDA
  N2: Raspberry_Pi_Zero1.GPIO3, Part2.SCL
  N3: Raspberry_Pi_Zero1.GPIO4, hc-sr1.Trig
  N4: Raspberry_Pi_Zero1.GPIO17, J1.pulse
  GND: Raspberry_Pi_Zero1.GPIO13, Raspberry_Pi_Zero1.GND, J1.gnd, S1.Pin_1, S1.Pin_2, S1.Pin_3, S1.Pin_4, J2.gnd, VCC1.-, Part1.GND, Part2.GND, hc-sr1.GND, R3.Pin_0, LED1.cathode, LED2.cathode, LED3.cathode, LED4.cathode
  VCC: Raspberry_Pi_Zero1.GPIO18, J1.vcc, J2.vcc, J2.pulse, Part1.VCC, Part2.VDD, hc-sr1.VCC, R4.pin_1, R5.pin_1, R6.pin_1, R7.Pin_0, R8.Pin_0, R9.Pin_0, R10.pin_1, R11.Pin_0
  N5: Raspberry_Pi_Zero1.GPIO14, R2.Pin_0, R3.Pin_1
  N6: VCC1.+, Part1.VIN
  N7: Part2.AIN3, R10.pin_0
  N8: Part2.AIN2, R6.pin_0
  N9: Part2.AIN1, R5.pin_0
  N10: Part2.AIN0, R4.pin_0
  N11: hc-sr1.Echo, R2.Pin_1
  N12: LED1.anode, R7.Pin_1
  N13: LED2.anode, R9.Pin_1
  N14: LED3.anode, R8.Pin_1
  N15: LED4.anode, R11.Pin_1

notes:
  5V
  FRONT
  LEFT
  RIGHT
  REAR

custom parts:
  Adafruit ADS1115 16Bit I2C ADC: For microcontrollers without an analog-to-digital converter or when you want a higher-precision ADC, the ADS1115 provides 16-bit precision at 860 samples/second over I2C. The chip can be configured as 4 single-ended input channels, or two differential channels. As a nice bonus, it even includes a programmable gain amplifier, up to x16, to help boost up smaller single/differential signals to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
